// Logisim project CircuitosSecuencials.circ as structural Verilog
module LatchRS (
  input  in_1,
  input  in_2,
  output out_3,
  output out_4
);

  nor nor_1 (out_3, in_2, out_4);
  nor nor_2 (out_4, out_3, in_1);
endmodule

module LatchD (
  input  in_1,
  input  in_2,
  output out_3,
  output out_4
);

  wire and_1_out, and_2_out, not_1_out;

  not not_1 (not_1_out, in_1);
  and and_1 (and_1_out, in_1, in_2);
  and and_2 (and_2_out, in_2, not_1_out);
  nor nor_1 (out_3, and_2_out, out_4);
  nor nor_2 (out_4, out_3, and_1_out);
endmodule

module FlipFlopD (
);

  D_Flip_Flop d_ff_1 ();  // open: D, clk, Q, Qn, preset, reset
endmodule

module FlipFlopJK (
);

  wire clock_1_out;

  J_K_Flip_Flop j_k_ff_1 (.clk(clock_1_out));  // open: J, K, Q, Qn, preset, reset
  Clock clock_1 (.out(clock_1_out));
endmodule

module E18registroDeSalidaRestringida (
  input  [3:0] in_1,
  input  WriteEnable,
  input  Reset,
  input  EnableOut,
  output [3:0] out_5
);

  wire and_1_out, Clk_out, d_ff_1_q, d_ff_2_q, d_ff_3_q, d_ff_4_q;

  Clock Clk (.out(Clk_out));
  and and_1 (and_1_out, Clk_out, WriteEnable);
  D_Flip_Flop d_ff_1 (.D(in_1[0]), .clk(and_1_out), .Q(d_ff_1_q), .reset(Reset));  // open: Qn, preset
  D_Flip_Flop d_ff_2 (.D(in_1[1]), .clk(and_1_out), .Q(d_ff_2_q), .reset(Reset));  // open: Qn, preset
  D_Flip_Flop d_ff_3 (.D(in_1[2]), .clk(and_1_out), .Q(d_ff_3_q), .reset(Reset));  // open: Qn, preset
  D_Flip_Flop d_ff_4 (.D(in_1[3]), .clk(and_1_out), .Q(d_ff_4_q), .reset(Reset));  // open: Qn, preset
  assign out_5[0] = EnableOut ? d_ff_1_q : 1'bz;  // Controlled_Buffer controlled_buffer_1
  assign out_5[1] = EnableOut ? d_ff_2_q : 1'bz;  // Controlled_Buffer controlled_buffer_2
  assign out_5[2] = EnableOut ? d_ff_3_q : 1'bz;  // Controlled_Buffer controlled_buffer_3
  assign out_5[3] = EnableOut ? d_ff_4_q : 1'bz;  // Controlled_Buffer controlled_buffer_4
endmodule

module E17extensorDeSigno (
  input  reset,
  input  we,
  input  [3:0] e,
  input  eo,
  output [3:0] out_5
);

  wire and_1_out, and_2_out, and_3_out, not_1_out, or_1_out, or_2_out;
  wire [3:0] e16registrosimple_1_out_4;

  E16registroSimple e16registrosimple_1 (.in_1(e), .WriteEnable(we), .Reset(reset), .out_4(e16registrosimple_1_out_4));
  not not_1 (not_1_out, eo);
  and and_1 (and_1_out, e16registrosimple_1_out_4[2], not_1_out);
  and and_2 (and_2_out, e16registrosimple_1_out_4[3], not_1_out);
  and and_3 (and_3_out, e16registrosimple_1_out_4[1], eo);
  or or_1 (or_1_out, and_1_out, and_3_out);
  or or_2 (or_2_out, and_3_out, and_2_out);
  Multiplexer multiplexer_1 (
    .in0(e16registrosimple_1_out_4[0]), .in1(e16registrosimple_1_out_4[0]), .out(out_5[0]), .sel(eo));
  Multiplexer multiplexer_2 (
    .in0(e16registrosimple_1_out_4[1]), .in1(e16registrosimple_1_out_4[1]), .out(out_5[1]), .sel(eo));
  Multiplexer multiplexer_3 (.in0(e16registrosimple_1_out_4[2]), .in1(or_1_out), .out(out_5[2]), .sel(eo));
  Multiplexer multiplexer_4 (.in0(e16registrosimple_1_out_4[3]), .in1(or_2_out), .out(out_5[3]), .sel(eo));
endmodule

module E16registroSimple (
  input  [3:0] in_1,
  input  WriteEnable,
  input  Reset,
  output [3:0] out_4
);

  wire and_1_out, Clk_out;

  Clock Clk (.out(Clk_out));
  and and_1 (and_1_out, Clk_out, WriteEnable);
  D_Flip_Flop d_ff_1 (.D(in_1[0]), .clk(and_1_out), .Q(out_4[0]), .reset(Reset));  // open: Qn, preset
  D_Flip_Flop d_ff_2 (.D(in_1[1]), .clk(and_1_out), .Q(out_4[1]), .reset(Reset));  // open: Qn, preset
  D_Flip_Flop d_ff_3 (.D(in_1[2]), .clk(and_1_out), .Q(out_4[2]), .reset(Reset));  // open: Qn, preset
  D_Flip_Flop d_ff_4 (.D(in_1[3]), .clk(and_1_out), .Q(out_4[3]), .reset(Reset));  // open: Qn, preset
endmodule
