// Logisim project A.B.C.circ as structural Verilog: 1 circuit, main circuit main
// A.B.C
module main (
);

  wire A_B_out, NOT__A_B_out, NOT_A_out, NOT_B_out, NOT_C_out, undriven, undriven_2, undriven_3;

  not NOT_A (NOT_A_out, undriven_3);
  not NOT_B (NOT_B_out, undriven_2);
  nor A_B (A_B_out, NOT_A_out, NOT_B_out);
  not NOT__A_B (NOT__A_B_out, A_B_out);
  not NOT_C (NOT_C_out, undriven);
  // NOR_Gate A_B_C has open pins: in0=NOT__A_B_out, in1=NOT_C_out, out=open

  // Notes on the sheet:
  //   C    B     A
endmodule
