// Logisim project A.B.circ as structural Verilog: 1 circuit, main circuit A.B
module A_B (
);

  wire A_B___A_B_out, A_B_out, undriven, undriven_2;

  nand A_B (A_B_out, undriven, undriven_2);
  nand A_B___A_B (A_B___A_B_out, A_B_out, A_B_out);

  // Notes on the sheet:
  //   A
  //   B
  //   A.B
endmodule
