// Logisim project SumCarry1Bit.circ as structural Verilog: 1 circuit, main circuit FullAdder1Bit
module FullAdder1Bit (
  input  Cin,
  input  B,
  input  A,
  output Sum,
  output Cout
);

  wire and_1_out, and_2_out, and_3_out, and_4_out, not_1_out, xnor_1_out, xor_1_out;

  xnor xnor_1 (xnor_1_out, B, A);
  not not_1 (not_1_out, Cin);
  xor xor_1 (xor_1_out, B, A);
  and and_1 (and_1_out, xnor_1_out, Cin);
  and and_2 (and_2_out, not_1_out, xor_1_out);
  and and_3 (and_3_out, xor_1_out, Cin);
  and and_4 (and_4_out, B, A);
  or or_1 (Sum, and_1_out, and_2_out);
  or or_2 (Cout, and_3_out, and_4_out);
endmodule
