// Logisim project SumCarry4Bits.circ as structural Verilog: 1 circuit, main circuit Sum&Carry
module Sum_Carry (
  input  Cin,
  input  A0,
  input  B0,
  input  A1,
  input  B1,
  input  A2,
  input  B2,
  input  A3,
  input  B3,
  output Sum0,
  output Sum1,
  output Sum2,
  output Sum3,
  output Cout
);

  wire and_1_out, and_2_out, and_3_out, and_4_out, and_5_out, and_6_out, and_7_out, and_8_out, and_9_out,
       and_10_out, and_11_out, and_12_out, and_13_out, and_14_out, and_15_out, and_16_out, not_1_out,
       not_2_out, not_3_out, not_4_out, or_2_out, or_4_out, or_6_out, xnor_1_out, xnor_2_out, xnor_3_out,
       xnor_4_out, xor_1_out, xor_2_out, xor_3_out, xor_4_out;

  xnor xnor_1 (xnor_1_out, A0, B0);
  not not_1 (not_1_out, Cin);
  xor xor_1 (xor_1_out, A0, B0);
  and and_1 (and_1_out, xnor_1_out, Cin);
  and and_2 (and_2_out, not_1_out, xor_1_out);
  and and_3 (and_3_out, xor_1_out, Cin);
  and and_4 (and_4_out, A0, B0);
  or or_1 (Sum0, and_1_out, and_2_out);
  or or_2 (or_2_out, and_3_out, and_4_out);
  xnor xnor_2 (xnor_2_out, A1, B1);
  not not_2 (not_2_out, or_2_out);
  xor xor_2 (xor_2_out, A1, B1);
  and and_5 (and_5_out, xnor_2_out, or_2_out);
  and and_6 (and_6_out, not_2_out, xor_2_out);
  and and_7 (and_7_out, xor_2_out, or_2_out);
  and and_8 (and_8_out, A1, B1);
  or or_3 (Sum1, and_5_out, and_6_out);
  or or_4 (or_4_out, and_7_out, and_8_out);
  xnor xnor_3 (xnor_3_out, A2, B2);
  not not_3 (not_3_out, or_4_out);
  xor xor_3 (xor_3_out, A2, B2);
  and and_9 (and_9_out, xnor_3_out, or_4_out);
  and and_10 (and_10_out, not_3_out, xor_3_out);
  and and_11 (and_11_out, xor_3_out, or_4_out);
  and and_12 (and_12_out, A2, B2);
  or or_5 (Sum2, and_9_out, and_10_out);
  or or_6 (or_6_out, and_11_out, and_12_out);
  xnor xnor_4 (xnor_4_out, A3, B3);
  not not_4 (not_4_out, or_6_out);
  xor xor_4 (xor_4_out, A3, B3);
  and and_13 (and_13_out, xnor_4_out, or_6_out);
  and and_14 (and_14_out, not_4_out, xor_4_out);
  and and_15 (and_15_out, xor_4_out, or_6_out);
  and and_16 (and_16_out, A3, B3);
  or or_7 (Sum3, and_13_out, and_14_out);
  or or_8 (Cout, and_15_out, and_16_out);
endmodule
