// Logisim project taller (1).circ as structural Verilog
module sumador_simple (
  input  A,
  input  B,
  output S,
  output Cout
);

  xor xor_1 (S, A, B);
  and and_1 (Cout, A, B);
endmodule

module sumador_completo (
  input  Cin,
  input  A,
  input  B,
  output S,
  output Cout
);

  wire sumador_simple_1_cout, sumador_simple_2_cout, sumador_simple_2_s;

  sumador_simple sumador_simple_1 (.A(Cin), .B(sumador_simple_2_s), .S(S), .Cout(sumador_simple_1_cout));
  sumador_simple sumador_simple_2 (.A(A), .B(B), .S(sumador_simple_2_s), .Cout(sumador_simple_2_cout));
  or or_1 (Cout, sumador_simple_1_cout, sumador_simple_2_cout);
endmodule

module sumador_4 (
  input  Cin,
  input  [3:0] A,
  input  [3:0] B,
  output [3:0] S,
  output Cout
);

  wire sumador_completo_1_cout, sumador_completo_2_cout, sumador_completo_3_cout;

  sumador_completo sumador_completo_1 (.Cin(Cin), .A(A[0]), .B(B[0]), .S(S[0]), .Cout(sumador_completo_1_cout));
  sumador_completo sumador_completo_2 (
    .Cin(sumador_completo_1_cout), .A(A[1]), .B(B[1]), .S(S[1]), .Cout(sumador_completo_2_cout));
  sumador_completo sumador_completo_3 (
    .Cin(sumador_completo_2_cout), .A(A[2]), .B(B[2]), .S(S[2]), .Cout(sumador_completo_3_cout));
  sumador_completo sumador_completo_4 (.Cin(sumador_completo_3_cout), .A(A[3]), .B(B[3]), .S(S[3]), .Cout(Cout));
  Hex_Digit_Display hex_digit_display_1 (.value(S));  // open: dp
endmodule

module comparador_cero (
  input  [3:0] A,
  output Z
);

  wire nor_1_out, nor_2_out;

  nor nor_1 (nor_1_out, A[0], A[1]);
  nor nor_2 (nor_2_out, A[2], A[3]);
  and and_1 (Z, nor_1_out, nor_2_out);
endmodule

module sumador_flags (
  input  Cin,
  input  [3:0] A,
  input  [3:0] B,
  output [3:0] S,
  output N,
  output Z,
  output V,
  output C
);

  wire and_1_out, and_2_out, and_3_out, and_4_out, not_1_out, not_2_out, not_3_out;

  not not_1 (not_1_out, A[3]);
  and and_1 (and_1_out, not_1_out, not_2_out);
  not not_2 (not_2_out, B[3]);
  and and_2 (and_2_out, A[3], B[3]);
  not not_3 (not_3_out, N);
  and and_3 (and_3_out, N, and_1_out);
  and and_4 (and_4_out, not_3_out, and_2_out);
  sumador_4 sumador_4_1 (.Cin(Cin), .A(A), .B(B), .S({N, S[2:0]}), .Cout(C));
  or or_1 (V, and_3_out, and_4_out);
  Hex_Digit_Display hex_digit_display_1 (.value({N, S[2:0]}));  // open: dp
  comparador_cero comparador_cero_1 (.A({N, S[2:0]}), .Z(Z));

  assign S[3] = N;
endmodule

module incrementador_4 (
  input  [3:0] A,
  output [3:0] S
);

  sumador_4 sumador_4_1 (.Cin(1'b1), .A(A), .S(S));  // open: B, Cout
  Hex_Digit_Display hex_digit_display_1 (.value(S));  // open: dp
endmodule

module inversor_4 (
  input  [3:0] A,
  input  INV,
  output [3:0] S
);

  wire and_1_out, and_2_out, and_3_out, and_4_out, and_5_out, and_6_out, and_7_out, and_8_out, not_5_out;
  wire [3:0] incrementador_4_1_s, not_1_out;

  not not_1 (not_1_out[0], A[0]);
  not not_2 (not_1_out[1], A[1]);
  not not_3 (not_1_out[2], A[2]);
  not not_4 (not_1_out[3], A[3]);
  incrementador_4 incrementador_4_1 (.A(not_1_out), .S(incrementador_4_1_s));
  and and_1 (and_1_out, incrementador_4_1_s[0], INV);
  and and_2 (and_2_out, incrementador_4_1_s[2], INV);
  and and_3 (and_3_out, incrementador_4_1_s[3], INV);
  not not_5 (not_5_out, INV);
  and and_4 (and_4_out, incrementador_4_1_s[1], INV);
  and and_5 (and_5_out, not_5_out, A[0]);
  and and_6 (and_6_out, A[1], not_5_out);
  and and_7 (and_7_out, A[2], not_5_out);
  and and_8 (and_8_out, A[3], not_5_out);
  or or_1 (S[0], and_5_out, and_1_out);
  or or_2 (S[1], and_6_out, and_4_out);
  or or_3 (S[2], and_7_out, and_2_out);
  or or_4 (S[3], and_8_out, and_3_out);
  Hex_Digit_Display hex_digit_display_1 (.value(S));  // open: dp
endmodule

module ALU (
  input  [3:0] A,
  input  [3:0] B,
  input  [1:0] OP,
  output N,
  output Z,
  output V,
  output C,
  output [3:0] S
);

  wire comparador_cero_1_z, comparador_cero_2_z, comparador_cero_3_z, not_1_out, sumador_flags_1_c,
       sumador_flags_1_n, sumador_flags_1_v, sumador_flags_1_z, sumador_flags_2_c, sumador_flags_2_n,
       sumador_flags_2_v, sumador_flags_2_z, xor_1_out;
  wire [3:0] aluand_1_out_3, aluor_1_out_3, inversor_4_1_s, sumador_flags_1_s, sumador_flags_2_s;

  sumador_flags sumador_flags_1 (
    .Cin(1'b0), .A(A), .B(B), .S(sumador_flags_1_s), .N(sumador_flags_1_n), .Z(sumador_flags_1_z),
    .V(sumador_flags_1_v), .C(sumador_flags_1_c));
  inversor_4 inversor_4_1 (.A(B), .INV(1'b1), .S(inversor_4_1_s));
  aluAND aluand_1 (.A(A), .B(B), .out_3(aluand_1_out_3));
  aluOR aluor_1 (.A(A), .B(B), .out_3(aluor_1_out_3));
  sumador_flags sumador_flags_2 (
    .Cin(1'b0), .A(A), .B(inversor_4_1_s), .S(sumador_flags_2_s), .N(sumador_flags_2_n),
    .Z(sumador_flags_2_z), .V(sumador_flags_2_v), .C(sumador_flags_2_c));
  not not_1 (not_1_out, sumador_flags_2_c);
  comparador_cero comparador_cero_1 (.A(aluand_1_out_3), .Z(comparador_cero_1_z));
  comparador_cero comparador_cero_2 (.A(aluor_1_out_3), .Z(comparador_cero_2_z));
  comparador_cero comparador_cero_3 (.A(B), .Z(comparador_cero_3_z));
  xor xor_1 (xor_1_out, not_1_out, comparador_cero_3_z);
  Multiplexer #(.select(2)) multiplexer_1 (
    .in0(sumador_flags_1_c), .in1(xor_1_out), .in2(1'b0), .in3(1'b0), .out(C), .sel(OP));
  Multiplexer #(.select(2)) multiplexer_2 (
    .in0(sumador_flags_1_v), .in1(sumador_flags_2_v), .in2(1'b0), .in3(1'b0), .out(V), .sel(OP));
  Multiplexer #(.select(2)) multiplexer_3 (
    .in0(sumador_flags_1_z), .in1(sumador_flags_2_z), .in2(comparador_cero_1_z), .in3(comparador_cero_2_z),
    .out(Z), .sel(OP));
  Multiplexer #(.select(2)) multiplexer_4 (
    .in0(sumador_flags_1_n), .in1(sumador_flags_2_n), .in2(aluand_1_out_3[0]), .in3(aluor_1_out_3[0]),
    .out(N), .sel(OP));
  Multiplexer #(.select(2), .width(4)) multiplexer_5 (
    .in0(sumador_flags_1_s), .in1(sumador_flags_2_s), .in2(aluand_1_out_3), .in3(aluor_1_out_3), .out(S),
    .sel(OP));
  Hex_Digit_Display hex_digit_display_1 (.value(S));  // open: dp
endmodule

module verificador (
  output [3:0] out_1,
  output [3:0] out_2,
  output [1:0] out_3,
  output halt,
  output N,
  output Z,
  output V,
  output C,
  output [3:0] res
);

  wire clock_1_out;

  Clock clock_1 (.out(clock_1_out));
  Counter #(.max('h3ff), .width(10)) counter_1 (
    .clk(clock_1_out), .carry(halt), .Q({out_3, out_2, out_1}));  // open: clr, load, up, count, D
  ALU alu_1 (.A(out_1), .B(out_2), .OP(out_3), .N(N), .Z(Z), .V(V), .C(C), .S(res));
endmodule

module overflow (
  input  in_1,
  output out_2
);

  wire and_1_out, nand_1_out, nor_1_out, nor_2_out, undriven, undriven_2;

  not nand_1 (nand_1_out, undriven);  // NAND_Gate
  not nor_1 (nor_1_out, undriven);  // NOR_Gate
  not nor_2 (nor_2_out, nand_1_out);  // NOR_Gate
  and and_1 (and_1_out, undriven_2, nor_1_out);
  // OR_Gate or_1 has open pins: in0=nor_2_out, in1=and_1_out, out=open
endmodule

module aluAND (
  input  [3:0] A,
  input  [3:0] B,
  output [3:0] out_3
);

  and and_1 (out_3[0], A[0], B[0]);
  and and_2 (out_3[1], A[1], B[1]);
  and and_3 (out_3[2], A[2], B[2]);
  and and_4 (out_3[3], A[3], B[3]);
endmodule

module aluOR (
  input  [3:0] A,
  input  [3:0] B,
  output [3:0] out_3
);

  or or_1 (out_3[0], A[0], B[0]);
  or or_2 (out_3[1], A[1], B[1]);
  or or_3 (out_3[2], A[2], B[2]);
  or or_4 (out_3[3], A[3], B[3]);
endmodule
